# Fritzing sketch setup (saved by Fritzing 0.9.3b)
breadboards: 1

parts:
  Bauteil1 = Arduino Uno (Rev3)
  LED1 = LED - 5mm [color="Red (633nm)" package="5 mm [THT]"]
  LED2 = LED - 5mm [color="Green (565nm)" package="5 mm [THT]"]
  LED3 = LED - 5mm [color="Blue (430nm)" package="5 mm [THT]"]
  LED4 = LED - 5mm [color="White (8000K)" package="5 mm [THT]"]
  R1 = Resistor [tolerance=±5% resistance=220 package=THT]
  R2 = Resistor [tolerance=±5% resistance=220 package=THT]
  R3 = Resistor [tolerance=±5% resistance=220 package=THT]
  R4 = Resistor [tolerance=±5% resistance=220 package=THT]
  S1 = Pushbutton [package="[THT]"]
  R5 = Resistor [tolerance=±5% resistance=220 package=THT]

nets:
  N1: Bauteil1.GND, R1.Pin_1, R2.Pin_1, R3.Pin_1, R4.Pin_1, R5.Pin_0
  N2: Bauteil1.D2, LED4.anode
  N3: Bauteil1.D3_PWM, LED3.anode
  N4: Bauteil1.D4, LED2.anode
  N5: Bauteil1.D5_PWM, LED1.anode
  N6: Bauteil1.D7, Bauteil1.5V, S1.Pin_1, S1.Pin_2
  N7: LED1.cathode, R4.Pin_0
  N8: LED2.cathode, R3.Pin_0
  N9: LED3.cathode, R2.Pin_0
  N10: LED4.cathode, R1.Pin_0
  N11: S1.Pin_3, S1.Pin_4, R5.Pin_1
